# Fritzing sketch ESP8266_Wifi_Lantern_Schematic (saved by Fritzing 0.9.6b)
breadboards: 1

parts:
  U1 = ESP8266 WiFi Module [part_number=ESP8266]
  HLK-PM2 = HLK-PM12 [part_number=HLK-PM12]
  Mod1 = VRM
  RGB_SMD_LED1 = SMD RGB LED (WS2812) [package=5050]

nets:
  N1: U1.D2, RGB_SMD_LED1.DIn
  N2: U1.GND#12, U1.GND#23, HLK-PM2.-Vo, Mod1.5V_500mA_GND1, Mod1.12V_2A_GND0, Mod1.12V_500mA_GND0, Mod1.InGnd, RGB_SMD_LED1.DOut
  N3: U1.3.3V#26, Mod1.5V_500mA_5V1
  N4: HLK-PM2.+Vo, Mod1.In12V
  N5: Mod1.12V_2A_12v0, RGB_SMD_LED1.VCC
